# Fritzing sketch emg wiring (saved by Fritzing 0.9.3b)
breadboards: 1

parts:
  Part1 = Arduino Uno (Rev3)
  U1 = POT_SWITCH [package=pot_pth]
  Part4 = MyoWare Cable Shield

nets:
  N1: Part1.A0, Part4.SIG
  N2: Part1.D9_PWM, U1.G$2_1
  5V: Part1.5V, U1.G$1_E, Part4.VCC
  GND: Part1.GND, U1.G$1_A, Part4.GND
